# Fritzing sketch switch-1129 (saved by Fritzing 0.9.4)
breadboards: 1

parts:
  Part1 = Bare Conductive Touch Board
  S1 = Toggle Switch [package=THT]
  R1 = Resistor [tolerance=±5% resistance=10k package="0805 [SMD]"]
  C1 = Electrolytic Capacitor [capacitance=0.1µF package="1010 [SMD, electrolytic]"]
  S2 = Toggle Switch [package=THT]
  R2 = Resistor [tolerance=±5% resistance=10k package="0805 [SMD]"]
  C2 = Electrolytic Capacitor [capacitance=0.1µF package="1010 [SMD, electrolytic]"]
  S3 = Toggle Switch [package=THT]
  R3 = Resistor [tolerance=±5% resistance=10k package="0805 [SMD]"]
  C3 = Electrolytic Capacitor [capacitance=0.1µF package="1010 [SMD, electrolytic]"]
  LED2 = LED - 5mm [color="Red (633nm)" package="5 mm [THT]"]
  R4 = Resistor [tolerance=±5% resistance=220 package=THT]

nets:
  N1: Part1.D3/SCL_PWM_(MPR121), R4.Pin_1
  N2: Part1.5V, S1.COM, S2.COM, S3.COM
  N3: Part1.GND, R1.Pin_1, C1.+, R2.Pin_1, C2.+, R3.Pin_1, C3.+, LED2.cathode
  N4: Part1.D11_PWM, S3.L2, R3.Pin_0, C3.-
  N5: Part1.D12/A11, S2.L2, R2.Pin_0, C2.-
  N6: Part1.D13_PWM, S1.L2, R1.Pin_0, C1.-
  N7: LED2.anode, R4.Pin_0
