# Fritzing sketch Untitled Sketch 6 (saved by Fritzing 0.9.4)
breadboards: 1

parts:
  Microcontroller = Arduino Uno (Rev3)
  RFID_reader = RFID-RC522-v2
  TimerLED1 = smd LED [color="Red (633nm)" package="1206 [SMD]"]
  TimerLED2 = smd LED [color="Yellow (595nm)" package="1206 [SMD]"]
  TimerLED3 = smd LED [color="Blue (525nm)" package="1206 [SMD]"]
  LED-RFID-reader = smd LED [color="Green (570nm)" package="1206 [SMD]"]
  R1 = Resistor [tolerance=±5% resistance=220 package=THT]
  R2 = Resistor [tolerance=±5% resistance=220 package=THT]
  R3 = Resistor [tolerance=±5% resistance=220 package=THT]
  R4 = Resistor [tolerance=±5% resistance=220 package=THT]

nets:
  N1: Microcontroller.D9_PWM, RFID_reader.MOSI
  N2: Microcontroller.D10_PWM/SS, RFID_reader.IRQ
  N3: Microcontroller.D11_PWM/MOSI, RFID_reader.GND
  N4: Microcontroller.D12/MISO, RFID_reader.SDA
  N5: Microcontroller.D13/SCK, RFID_reader.SCK
  N6: Microcontroller.GND, RFID_reader.RST, R1.Pin_1, R2.Pin_1, R3.Pin_1, R4.Pin_1
  N7: Microcontroller.D2, LED-RFID-reader.anode
  N8: Microcontroller.D4, TimerLED1.anode
  N9: Microcontroller.D5_PWM, TimerLED2.anode
  N10: Microcontroller.D6_PWM, TimerLED3.anode
  N11: Microcontroller.3V3, RFID_reader.3_3V
  N12: TimerLED1.cathode, R2.Pin_0
  N13: TimerLED2.cathode, R3.Pin_0
  N14: TimerLED3.cathode, R4.Pin_0
  N15: LED-RFID-reader.cathode, R1.Pin_0

notes:
  TX-O-RS232 = SDA:10
  TX-O = MOSI:11
  GNDT = MISO:12
  CP = SCK:13
  ANT2 = RST: 9
  VCC = 3.3V
  GND
  LED-RFIDReader(Green) - 2
  LED-Timer1(Red)-4
  LED-Timer2(Yellow)-5
  LED-Timer3(Blue)-6

custom parts:
  RFID-RC522-v2: A simple China made RFID-RC522 Reader; do check the pin labels, as this is a MFRC522 based clone.
